// Logisim project arav.circ as structural Verilog: 9 circuits, main circuit main
module main (
  input  in_1,
  output out_2
);

  // AND_Gate iiii is placed but not wired

  assign out_2 = in_1;
endmodule

module mmmm (
);

  main main_1 ();  // open: in_1, out_2
  // OR_Gate or_1 is placed but not wired
  // AND_Gate and_1 is placed but not wired
  main main_2 ();  // open: in_1, out_2
endmodule

module RS (
  input  S,
  input  R,
  output Q,
  output Q_2
);

  nor nor_1 (Q, S, Q_2);
  nor nor_2 (Q_2, Q, R);
endmodule

module d_latch (
  input  in_1,
  input  in_2,
  output out_3,
  output out_4
);

  wire and_1_out, and_2_out, not_1_out;

  not not_1 (not_1_out, in_2);
  and and_1 (and_1_out, in_1, not_1_out);
  and and_2 (and_2_out, in_1, in_2);
  RS rs_1 (.S(and_1_out), .R(and_2_out), .Q(out_3), .Q_2(out_4));
endmodule

module d_flip_flop (
  input  in_1,
  input  in_2,
  output out_3,
  output out_4
);

  wire d_latch_1_out_3, not_1_out;

  not not_1 (not_1_out, in_1);
  d_latch d_latch_1 (.in_1(in_1), .in_2(in_2), .out_3(d_latch_1_out_3));  // open: out_4
  d_latch d_latch_2 (.in_1(not_1_out), .in_2(d_latch_1_out_3), .out_3(out_3), .out_4(out_4));
endmodule

module register (
  input  in_1,
  input  in_2,
  input  in_3,
  input  in_4,
  input  in_5,
  input  in_6,
  input  in_7,
  input  in_8,
  input  in_9,
  input  in_10
);

  wire and_1_out, and_2_out, and_3_out, and_4_out, d_flip_flop_1_out_3, d_flip_flop_2_out_3,
       d_flip_flop_3_out_3, d_flip_flop_4_out_3;

  and and_1 (and_1_out, in_2, in_4);
  and and_2 (and_2_out, in_2, in_6);
  and and_3 (and_3_out, in_2, in_8);
  and and_4 (and_4_out, in_2, in_10);
  d_flip_flop d_flip_flop_1 (.in_1(in_1), .in_2(and_1_out), .out_3(d_flip_flop_1_out_3));  // open: out_4
  d_flip_flop d_flip_flop_2 (.in_1(in_1), .in_2(and_2_out), .out_3(d_flip_flop_2_out_3));  // open: out_4
  d_flip_flop d_flip_flop_3 (.in_1(in_1), .in_2(and_3_out), .out_3(d_flip_flop_3_out_3));  // open: out_4
  d_flip_flop d_flip_flop_4 (.in_1(in_1), .in_2(and_4_out), .out_3(d_flip_flop_4_out_3));  // open: out_4
endmodule

module reg_file (
  input  in_1,
  input  _10,
  input  _111
);

  wire undriven;

  Demultiplexer demultiplexer_1 (.sel(_10), .en(undriven));  // open: out0, out1, in
  register register_1 (
    .in_1(in_1), .in_2(_111), .in_3(_111), .in_4(_111), .in_5(_111));  // open: in_6, in_7, in_8, in_9, in_10
  register register_2 (
    .in_1(in_1), .in_2(_111), .in_3(_111), .in_4(_111), .in_5(_111));  // open: in_6, in_7, in_8, in_9, in_10
  register register_3 (
    .in_1(in_1), .in_2(_111), .in_3(_111), .in_4(_111), .in_5(_111));  // open: in_6, in_7, in_8, in_9, in_10
  register register_4 (
    .in_1(in_1), .in_2(_111), .in_3(_111), .in_4(_111), .in_5(_111));  // open: in_6, in_7, in_8, in_9, in_10
  Demultiplexer demultiplexer_2 (.en(undriven));  // open: out0, out1, in, sel
endmodule

module multiplexer (
  input  in_1,
  input  in_2,
  input  in_3,
  output out_4
);

  wire and_1_out, and_2_out, not_1_out;

  not not_1 (not_1_out, in_3);
  and and_1 (and_1_out, in_1, not_1_out);
  and and_2 (and_2_out, in_2, in_3);
  or or_1 (out_4, and_1_out, and_2_out);
endmodule

module test (
  input  in_1,
  input  in_2,
  input  in_3,
  input  in_4,
  output out_5
);

  wire multiplexer_1_out_4, multiplexer_2_out_4, undriven;

  multiplexer multiplexer_1 (.in_1(in_1), .in_2(in_1), .out_4(multiplexer_1_out_4), .in_3(undriven));
  multiplexer multiplexer_2 (.in_1(in_2), .in_2(in_2), .out_4(multiplexer_2_out_4), .in_3(undriven));
  multiplexer multiplexer_3 (.in_1(multiplexer_1_out_4), .in_2(multiplexer_2_out_4), .out_4(out_5), .in_3(in_3));
endmodule
