// Logisim project lv10mux.circ as structural Verilog: 2 circuits, main circuit mux_2x1
module mux_2x1 (
  input  A0,
  input  A1,
  input  S0,
  output out_4
);

  wire and_1_out, and_2_out, not_1_out;

  not not_1 (not_1_out, S0);
  and and_1 (and_1_out, A0, not_1_out);
  and and_2 (and_2_out, A1, S0);
  or or_1 (out_4, and_1_out, and_2_out);
endmodule

module mux_4x1 (
  input  [1:0] in_1,
  input  [1:0] in_2,
  input  in_3,
  input  in_4,
  output out_5
);

  wire mux_2x1_1_out_4, mux_2x1_2_out_4;

  mux_2x1 mux_2x1_1 (.out_4(mux_2x1_1_out_4), .S0(in_4), .A1(in_1[1]), .A0(in_1[0]));
  mux_2x1 mux_2x1_2 (.out_4(mux_2x1_2_out_4), .S0(in_4), .A1(in_2[1]), .A0(in_2[0]));
  mux_2x1 mux_2x1_3 (.out_4(out_5), .S0(in_3), .A1(mux_2x1_2_out_4), .A0(mux_2x1_1_out_4));
endmodule
