// Logisim project lv10register.circ as structural Verilog: 5 circuits, main circuit RSLatch
module RSLatch (
  input  in_1,
  input  in_2,
  output out_3,
  output out_4
);

  nor nor_1 (out_3, in_1, out_4);
  nor nor_2 (out_4, out_3, in_2);
endmodule

module DLatch (
  input  in_1,
  input  in_2,
  output out_3,
  output out_4
);

  wire and_1_out, and_2_out, not_1_out;

  not not_1 (not_1_out, in_2);
  and and_1 (and_1_out, in_1, not_1_out);
  and and_2 (and_2_out, in_1, in_2);
  RSLatch rslatch_1 (.out_4(out_4), .in_2(and_2_out), .in_1(and_1_out), .out_3(out_3));
endmodule

module DFlipFlop (
  input  in_1,
  input  in_2,
  output out_3,
  output out_4
);

  wire dlatch_1_out_3, not_1_out;

  not not_1 (not_1_out, in_1);
  DLatch dlatch_1 (.in_2(in_2), .in_1(in_1), .out_3(dlatch_1_out_3));  // open: out_4
  DLatch dlatch_2 (.out_4(out_4), .in_2(dlatch_1_out_3), .in_1(not_1_out), .out_3(out_3));
endmodule

module Reg4 (
  input  in_1,
  input  in_2,
  input  in_3,
  input  in_4,
  input  in_5,
  input  in_6,
  output out_7,
  output out_8,
  output out_9,
  output out_10
);

  wire and_1_out, and_2_out, and_3_out, and_4_out;

  and and_1 (and_1_out, in_2, in_3);
  and and_2 (and_2_out, in_2, in_4);
  and and_3 (and_3_out, in_2, in_5);
  and and_4 (and_4_out, in_2, in_6);
  DFlipFlop dflipflop_1 (.in_2(and_1_out), .in_1(in_1), .out_3(out_7));  // open: out_4
  DFlipFlop dflipflop_2 (.in_2(and_2_out), .in_1(in_1), .out_3(out_8));  // open: out_4
  DFlipFlop dflipflop_3 (.in_2(and_3_out), .in_1(in_1), .out_3(out_9));  // open: out_4
  DFlipFlop dflipflop_4 (.in_2(and_4_out), .in_1(in_1), .out_3(out_10));  // open: out_4
endmodule

module RegFile (
  input  in_1,
  input  [1:0] in_2,
  input  [1:0] in_3,
  input  [3:0] in_4,
  output [3:0] out_5
);

  wire decoder_1_out0, decoder_1_out1, decoder_1_out2, decoder_1_out3, decoder_2_out0, decoder_2_out1,
       decoder_2_out2, decoder_2_out3;
  wire [3:0] reg4_1_out_7, reg4_2_out_7, reg4_3_out_7, reg4_4_out_7;

  Decoder #(.select(2)) decoder_1 (
    .out0(decoder_1_out0), .out1(decoder_1_out1), .out2(decoder_1_out2), .out3(decoder_1_out3), .sel(in_2),
    .en(1'b1));
  Reg4 reg4_1 (
    .out_8(reg4_1_out_7[1]), .out_7(reg4_1_out_7[0]), .in_6(in_4[3]), .in_5(in_4[2]), .in_4(in_4[1]),
    .in_3(in_4[0]), .in_1(in_1), .out_9(reg4_1_out_7[2]), .out_10(reg4_1_out_7[3]), .in_2(decoder_1_out0));
  Reg4 reg4_2 (
    .out_8(reg4_2_out_7[1]), .out_7(reg4_2_out_7[0]), .in_6(in_4[3]), .in_5(in_4[2]), .in_4(in_4[1]),
    .in_3(in_4[0]), .in_1(in_1), .out_9(reg4_2_out_7[2]), .out_10(reg4_2_out_7[3]), .in_2(decoder_1_out1));
  Reg4 reg4_3 (
    .out_8(reg4_3_out_7[1]), .out_7(reg4_3_out_7[0]), .in_6(in_4[3]), .in_5(in_4[2]), .in_4(in_4[1]),
    .in_3(in_4[0]), .in_1(in_1), .out_9(reg4_3_out_7[2]), .out_10(reg4_3_out_7[3]), .in_2(decoder_1_out2));
  Reg4 reg4_4 (
    .out_8(reg4_4_out_7[1]), .out_7(reg4_4_out_7[0]), .in_6(in_4[3]), .in_5(in_4[2]), .in_4(in_4[1]),
    .in_3(in_4[0]), .in_1(in_1), .out_9(reg4_4_out_7[2]), .out_10(reg4_4_out_7[3]), .in_2(decoder_1_out3));
  Decoder #(.select(2)) decoder_2 (
    .out0(decoder_2_out0), .out1(decoder_2_out1), .out2(decoder_2_out2), .out3(decoder_2_out3), .sel(in_3),
    .en(1'b1));
  assign out_5 = decoder_2_out3 ? reg4_4_out_7 : 4'bz;  // Controlled_Buffer controlled_buffer_1
  assign out_5 = decoder_2_out0 ? reg4_1_out_7 : 4'bz;  // Controlled_Buffer controlled_buffer_2
  assign out_5 = decoder_2_out1 ? reg4_2_out_7 : 4'bz;  // Controlled_Buffer controlled_buffer_3
  assign out_5 = decoder_2_out2 ? reg4_3_out_7 : 4'bz;  // Controlled_Buffer controlled_buffer_4
endmodule
