// Logisim project sabirac.circ as structural Verilog: 2 circuits, main circuit sabirac1bit
module sabirac1bit (
  input  a,
  input  b,
  input  prenos,
  output rezultat,
  output prenos1
);

  wire and_1_out, and_2_out, xor_1_out;

  xor xor_1 (xor_1_out, a, b);
  // Probe on rezultat
  and and_1 (and_1_out, a, b);
  and and_2 (and_2_out, xor_1_out, prenos);
  xor xor_2 (rezultat, xor_1_out, prenos);
  or or_1 (prenos1, and_1_out, and_2_out);
endmodule

module sabirac4bit (
  input  in_1,
  input  [3:0] a,
  input  [3:0] b,
  output [3:0] rezultat,
  output prenos
);

  wire sabirac1bit_1_p5, sabirac1bit_2_p5, sabirac1bit_3_p5;

  // sabirac1bit sabirac1bit_1: pin names not known; wires that end beside it: a[0], b[0], in_1, rezultat[0], sabirac1bit_1_p5
  // sabirac1bit sabirac1bit_2: pin names not known; wires that end beside it: a[1], b[1], sabirac1bit_1_p5, rezultat[1], sabirac1bit_2_p5
  // sabirac1bit sabirac1bit_3: pin names not known; wires that end beside it: a[2], b[2], sabirac1bit_2_p5, rezultat[2], sabirac1bit_3_p5
  // sabirac1bit sabirac1bit_4: pin names not known; wires that end beside it: a[3], b[3], sabirac1bit_3_p5, rezultat[3], prenos
  Hex_Digit_Display hex_digit_display_1 (.value(rezultat));  // open: dp
endmodule
